# Fritzing sketch all (saved by Fritzing 0.8.7b)
breadboards: 1

parts:
  Part1 = Arduino Uno (Rev3)
  Part2 = Triple Axis Magnetometer - HMC5883 Breakout
  U3 = mystery part, 3 pins [chip_label=?]
  U4 = mystery part, 3 pins [chip_label=?]
  R3 = Resistor [tolerance=±5% resistance=220 package=THT]
  R4 = Resistor [tolerance=±5% resistance=220 package=THT]

nets:
  N1: Part1.A4/SDA, Part2.SDA
  N2: Part1.A5/SCL, Part2.SCL
  N3: Part1.D3_PWM, U3.pin2
  N4: Part1.D4, R4.Pin_0
  5V: Part1.5V, Part2.VCC, U4.pin1
  GND: Part1.GND, Part2.GND, U3.pin3, R3.Pin_0
  N5: U3.pin1, R3.Pin_1, R4.Pin_1

notes:
  <-- Compass
  <-- GPS
