# Fritzing sketch gps (saved by Fritzing 0.8.7b)
breadboards: 1

parts:
  Part1 = Arduino Uno (Rev3)
  U1 = mystery part, 3 pins [chip_label=?]
  U2 = mystery part, 3 pins [chip_label=?]
  R1 = Resistor [tolerance=±5% resistance=220 package=THT]
  R2 = Resistor [tolerance=±5% resistance=220 package=THT]

nets:
  N1: Part1.D6_PWM, U1.pin2
  N2: Part1.D7, R2.Pin_0
  N3: Part1.5V, U2.pin1
  N4: Part1.GND, U1.pin3, R1.Pin_0
  N5: U1.pin1, R1.Pin_1, R2.Pin_1

notes:
  GPS
  <-- GPS
