# Fritzing sketch sensors-v3 (saved by Fritzing 0.8.7b)
breadboards: 1

parts:
  Part1 = Arduino Uno (Rev3)
  U5 = mystery part, 3 pins [chip_label=?]
  U6 = mystery part, 3 pins [chip_label=?]
  R1 = Resistor [tolerance=±5% resistance=220 package=THT]
  R2 = Resistor [tolerance=±5% resistance=220 package=THT]
  Part2 = Triple Axis Magnetometer - HMC5883 Breakout  # not connected

nets:
  N1: Part1.D3_PWM, U5.pin2
  N2: Part1.D4, R1.Pin_1
  N3: Part1.3V3, U6.pin1, U6.pin2
  N4: Part1.GND, U5.pin3, R2.Pin_1
  N5: U5.pin1, R1.Pin_0, R2.Pin_0

notes:
  UP501
  GPS
  1. RX
  2. TX
  3. GND
  4. +3.3V
  5. Backup Pwr
  6. Timing Pulse
  HMC5883L
  Compass
  1. +5V
  2. GND
  3. SCL -> A5
  4. SDA -> A4
